# Fritzing sketch Arduino-Arduino_I2C (saved by Fritzing 0.9.3b)
breadboards: 2

parts:
  パーツ1 = Arduino Pro Mini (3.3V)
  パーツ2 = Arduino Pro Mini (3.3V)
  Power_plug1 = Power plug  # not connected
  パーツ3 = Arduino Pro Mini (3.3V)
  パーツ4 = Arduino Pro Mini (3.3V)
  Power_plug2 = Power plug
  R1 = Resistor [tolerance=±5% resistance=2.2k package=THT]
  R2 = Resistor [tolerance=±5% resistance=2.2k package=THT]

nets:
  N1: パーツ1.A4, パーツ2.A4
  N2: パーツ1.A5, パーツ2.A5
  N3: パーツ3.A4, パーツ4.A4, R1.Pin_0
  N4: パーツ3.A5, パーツ4.A5, R2.Pin_0
  N5: Power_plug2.VCC, R1.Pin_1, R2.Pin_1

notes:
  Direct
  Pullup
  3.3V
